# Fritzing sketch AG1v3.0 schematic (saved by Fritzing 0.7.0b)
breadboards: 1

parts:
  Part1 = Arduino 101
  Part4 = FC-28 Soil Hygrometer Module - Probe
  Part5 = FC-28 Soil Hygrometer Module - Probe
  Part6 = FC-28 Soil Hygrometer Module
  Part7 = FC-28 Soil Hygrometer Module
  R1 = Resistor [tolerance=±5% resistance=330 package=THT]
  R2 = Resistor [tolerance=±5% resistance=330 package=THT]
  R3 = Resistor [tolerance=±5% resistance=330 package=THT]
  R4 = Resistor [tolerance=±5% resistance=330 package=THT]
  LED1 = LED - 5mm [color="Red (633nm)" package="5 mm [THT]"]
  LED2 = LED - 5mm [color="Red (633nm)" package="5 mm [THT]"]
  LED3 = LED - 5mm [color="Green (570nm)" package="5 mm [THT]"]
  LED4 = LED - 5mm [color="Green (570nm)" package="5 mm [THT]"]
  LCD1 = LCD screen  # not connected
  LCM1602_IIC1 = LCM1602 IIC [part_number="LCM1602 IIC" chip_label="LCM1602 IIC" spacing=300mil package="DIP (Dual Inline) [THT]"]
  DHT1 = DHT11 Humitidy and Temperature Sensor  # not connected

nets:
  N1: Part1.A0, Part6.AO
  N2: Part1.A1, Part7.AO
  N3: Part1.D8, R3.Pin_0
  N4: Part1.D9_PWM, R4.Pin_0
  GND: Part1.GND, Part6.GND, Part7.GND, R1.Pin_1, R2.Pin_1, R3.Pin_1, R4.Pin_1, LED1.cathode, LED1.anode, LED2.cathode, LED2.anode, LED3.cathode, LED3.anode, LED4.cathode, LED4.anode, LCM1602_IIC1.GND
  N5: Part1.D6_PWM, R2.Pin_0
  N6: Part1.D7, R1.Pin_0
  VCC: Part1.3V3, Part6.VCC, Part7.VCC, LCM1602_IIC1.VCC
  N7: Part4.POS, Part7.POS
  N8: Part4.NEG, Part7.NEG
  N9: Part5.POS, Part6.POS
  N10: Part5.NEG, Part6.NEG

custom parts:
  Arduino 101: A learning and development board that delivers the performance and low-power consumption of the Intel® Curie™ Module with the simplicity of Arduino at an entry-level price. It keeps the same robust form factor and peripheral list of the UNO with the addition of onboard Bluetooth LE capabilities and a 6-axis accelerometer/gyro to help you easily expand your creativity into the connected world.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
  FC-28 Soil Hygrometer Module - Probe: The FC-28 is a soil hygrometer module that uses the Texas Instruments LM393 comparator chip to provide an analog measurement of soil humidity.
  FC-28 Soil Hygrometer Module: The FC-28 is a soil hygrometer module that uses the Texas Instruments LM393 comparator chip to provide an analog measurement of soil humidity. The digital output is high when soil moisture is over a certain threshold, as determined by adjusting the potentiometer.
  LCM1602 IIC: I2C-Module to use a 1602 or 2004 LCD on with the wire.h libory Serial LCD Modul
  DHT11 Humitidy and Temperature Sensor: DHT11 Humidity and Temperature Sensor
